// Logisim project tic-tac-toe-logic.circ as structural Verilog: 1 circuit, main circuit main
module main (
  input  in_1,
  input  in_2,
  input  in_3,
  input  in_4,
  input  in_5,
  input  in_6,
  input  in_7,
  input  in_8,
  input  in_9,
  output Result
);

  wire and_1_out, and_2_out, and_3_out, and_4_out, and_5_out, and_6_out, and_7_out, and_8_out, or_1_out,
       or_2_out;

  and and_1 (and_1_out, in_1, in_4, in_7);
  and and_2 (and_2_out, in_2, in_5, in_8);
  and and_3 (and_3_out, in_3, in_6, in_9);
  and and_4 (and_4_out, in_1, in_2, in_3);
  and and_5 (and_5_out, in_4, in_5, in_6);
  and and_6 (and_6_out, in_7, in_8, in_9);
  and and_7 (and_7_out, in_1, in_5, in_9);
  and and_8 (and_8_out, in_7, in_5, in_3);
  or or_1 (or_1_out, and_4_out, and_5_out, and_6_out, and_7_out);
  or or_2 (or_2_out, and_8_out, and_1_out, and_2_out, and_3_out);
  or or_3 (Result, or_1_out, or_2_out);

  // Notes on the sheet:
  //   Column 1
  //   Column 2
  //   Column 3
  //   Row 1
  //   Row 2
  //   Row 3
  //   Diag L
  //   Diag R
endmodule
